// Logisim project SomadorSubtrator8bit.circ as structural Verilog: 6 circuits, main circuit somador1bit
module main (
  input  in_1,
  input  in_2,
  input  in_3,
  input  in_4,
  input  in_5,
  input  in_6,
  input  in_7,
  input  in_8,
  input  in_9,
  input  in_10,
  input  in_11,
  input  in_12,
  input  in_13,
  input  in_14,
  input  in_15,
  input  in_16,
  input  in_17,
  input  in_18,
  input  in_19,
  input  in_20,
  input  in_21,
  input  in_22,
  input  in_23,
  input  in_24,
  input  in_25,
  input  in_26,
  input  in_27,
  input  in_28,
  input  in_29,
  input  in_30,
  input  in_31,
  input  in_32,
  input  in_33,
  input  sub,
  output out_35,
  output out_36,
  output out_37,
  output out_38,
  output out_39,
  output out_40,
  output out_41,
  output out_42,
  output out_43,
  output out_44,
  output out_45,
  output out_46,
  output out_47,
  output out_48,
  output out_49,
  output out_50,
  output out_51,
  output out_52
);

  somadorSub8bit somadorsub8bit_1 (
    .sub(sub), .b7(in_25), .a7(in_9), .b6(in_26), .a6(in_10), .b5(in_27), .a5(in_11), .b4(in_28), .a4(in_12),
    .b3(in_29), .a3(in_13), .b2(in_30), .a2(in_14), .b1(in_31), .a1(in_15), .b0(in_32), .a0(in_16),
    .c7(out_45), .c6(out_46), .c5(out_47), .c4(out_48), .c3(out_49), .c2(out_50), .c1(out_51), .c0(out_52),
    .cout(out_36));
  somador8bit somador8bit_1 (
    .cin(in_33), .b7(in_17), .a7(in_1), .b6(in_18), .a6(in_2), .b5(in_19), .a5(in_3), .b4(in_20), .a4(in_4),
    .b3(in_21), .a3(in_5), .b2(in_22), .a2(in_6), .b1(in_23), .a1(in_7), .b0(in_24), .a0(in_8), .c7(out_37),
    .c6(out_38), .c5(out_39), .c4(out_40), .c3(out_41), .c2(out_42), .c1(out_43), .c0(out_44), .cout(out_35));
endmodule

module somador1bit (
  input  a,
  input  b,
  input  cin,
  output s,
  output cout
);

  wire and_1_out, and_2_out, and_3_out, xor_1_out;

  xor xor_1 (xor_1_out, a, b);
  and and_1 (and_1_out, a, b);
  and and_2 (and_2_out, a, cin);
  and and_3 (and_3_out, b, cin);
  xor xor_2 (s, xor_1_out, cin);
  or or_1 (cout, and_1_out, and_2_out, and_3_out);
endmodule

module somador4bit (
  input  cin,
  input  b3,
  input  a3,
  input  b2,
  input  a2,
  input  b1,
  input  a1,
  input  b0,
  input  a0,
  output c3,
  output c2,
  output c1,
  output c0,
  output cout
);

  wire somador1bit_2_cout, somador1bit_3_cout, somador1bit_4_cout;

  somador1bit somador1bit_1 (.a(a3), .b(b3), .cin(somador1bit_2_cout), .s(c3), .cout(cout));
  somador1bit somador1bit_2 (.a(a2), .b(b2), .cin(somador1bit_3_cout), .s(c2), .cout(somador1bit_2_cout));
  somador1bit somador1bit_3 (.a(a1), .b(b1), .cin(somador1bit_4_cout), .s(c1), .cout(somador1bit_3_cout));
  somador1bit somador1bit_4 (.a(a0), .b(b0), .cin(cin), .s(c0), .cout(somador1bit_4_cout));
endmodule

module somador8bit (
  input  cin,
  input  b7,
  input  a7,
  input  b6,
  input  a6,
  input  b5,
  input  a5,
  input  b4,
  input  a4,
  input  b3,
  input  a3,
  input  b2,
  input  a2,
  input  b1,
  input  a1,
  input  b0,
  input  a0,
  output c7,
  output c6,
  output c5,
  output c4,
  output c3,
  output c2,
  output c1,
  output c0,
  output cout
);

  wire somador4bit_2_cout;

  somador4bit somador4bit_1 (
    .cin(somador4bit_2_cout), .b3(b7), .a3(a7), .b2(b6), .a2(a6), .b1(b5), .a1(a5), .b0(b4), .a0(a4),
    .c3(c7), .c2(c6), .c1(c5), .c0(c4), .cout(cout));
  somador4bit somador4bit_2 (
    .cin(cin), .b3(b3), .a3(a3), .b2(b2), .a2(a2), .b1(b1), .a1(a1), .b0(b0), .a0(a0), .c3(c3), .c2(c2),
    .c1(c1), .c0(c0), .cout(somador4bit_2_cout));
endmodule

module somadorSub8bit (
  input  sub,
  input  b7,
  input  a7,
  input  b6,
  input  a6,
  input  b5,
  input  a5,
  input  b4,
  input  a4,
  input  b3,
  input  a3,
  input  b2,
  input  a2,
  input  b1,
  input  a1,
  input  b0,
  input  a0,
  output c7,
  output c6,
  output c5,
  output c4,
  output c3,
  output c2,
  output c1,
  output c0,
  output cout
);

  wire not_1_out, not_2_out, not_3_out, not_4_out, not_5_out, not_6_out, not_7_out, not_8_out,
       seletor1bit_1_out_4, seletor1bit_2_out_4, seletor1bit_3_out_4, seletor1bit_4_out_4,
       seletor1bit_5_out_4, seletor1bit_6_out_4, seletor1bit_7_out_4, seletor1bit_8_out_4;

  not not_1 (not_1_out, b7);
  not not_2 (not_2_out, b6);
  not not_3 (not_3_out, b5);
  not not_4 (not_4_out, b4);
  not not_5 (not_5_out, b3);
  not not_6 (not_6_out, b2);
  not not_7 (not_7_out, b1);
  not not_8 (not_8_out, b0);
  seletor1bit seletor1bit_1 (.S(sub), .a0(b7), .a1(not_1_out), .out_4(seletor1bit_1_out_4));
  seletor1bit seletor1bit_2 (.S(sub), .a0(b6), .a1(not_2_out), .out_4(seletor1bit_2_out_4));
  seletor1bit seletor1bit_3 (.S(sub), .a0(b5), .a1(not_3_out), .out_4(seletor1bit_3_out_4));
  seletor1bit seletor1bit_4 (.S(sub), .a0(b4), .a1(not_4_out), .out_4(seletor1bit_4_out_4));
  seletor1bit seletor1bit_5 (.S(sub), .a0(b3), .a1(not_5_out), .out_4(seletor1bit_5_out_4));
  seletor1bit seletor1bit_6 (.S(sub), .a0(b2), .a1(not_6_out), .out_4(seletor1bit_6_out_4));
  seletor1bit seletor1bit_7 (.S(sub), .a0(b1), .a1(not_7_out), .out_4(seletor1bit_7_out_4));
  seletor1bit seletor1bit_8 (.S(sub), .a0(b0), .a1(not_8_out), .out_4(seletor1bit_8_out_4));
  somador8bit somador8bit_1 (
    .cin(sub), .b7(seletor1bit_1_out_4), .a7(a7), .b6(seletor1bit_2_out_4), .a6(a6),
    .b5(seletor1bit_3_out_4), .a5(a5), .b4(seletor1bit_4_out_4), .a4(a4), .b3(seletor1bit_5_out_4), .a3(a3),
    .b2(seletor1bit_6_out_4), .a2(a2), .b1(seletor1bit_7_out_4), .a1(a1), .b0(seletor1bit_8_out_4), .a0(a0),
    .c7(c7), .c6(c6), .c5(c5), .c4(c4), .c3(c3), .c2(c2), .c1(c1), .c0(c0), .cout(cout));
endmodule

module seletor1bit (
  input  S,
  input  a0,
  input  a1,
  output out_4
);

  wire and_1_out, and_2_out, not_1_out;

  not not_1 (not_1_out, S);
  and and_1 (and_1_out, not_1_out, a0);
  and and_2 (and_2_out, S, a1);
  or or_1 (out_4, and_1_out, and_2_out);
endmodule
