// Logisim project somador8_Cristian_Fraporti.circ as structural Verilog: 4 circuits, main circuit somador_1
module somador_1 (
  input  A,
  input  B,
  input  Cin,
  output S,
  output Cout
);

  wire and_1_out, and_2_out, and_3_out, xor_1_out;

  xor xor_1 (xor_1_out, A, B);
  and and_1 (and_1_out, A, B);
  and and_2 (and_2_out, A, Cin);
  and and_3 (and_3_out, B, Cin);
  xor xor_2 (S, xor_1_out, Cin);
  or or_1 (Cout, and_1_out, and_2_out, and_3_out);
endmodule

module somador_2 (
  input  A0,
  input  B0,
  input  Cin,
  input  A1,
  input  B1,
  output S0,
  output S1,
  output Cout
);

  wire somador_1_1_cout;

  somador_1 somador_1_1 (.A(A0), .B(B0), .Cin(Cin), .S(S0), .Cout(somador_1_1_cout));
  somador_1 somador_1_2 (.A(A1), .B(B1), .Cin(somador_1_1_cout), .S(S1), .Cout(Cout));
endmodule

module somador_4 (
  input  A0,
  input  A1,
  input  A2,
  input  A3,
  input  B0,
  input  B1,
  input  B2,
  input  B3,
  input  Cin,
  output S0,
  output S1,
  output S2,
  output S3,
  output Cout
);

  wire somador_2_1_cout;

  somador_2 somador_2_1 (.A0(A0), .B0(B0), .A1(A1), .B1(B1), .S0(S0), .S1(S1), .Cout(somador_2_1_cout), .Cin(Cin));
  somador_2 somador_2_2 (.A0(A2), .B0(B2), .A1(A3), .B1(B3), .S0(S2), .S1(S3), .Cout(Cout), .Cin(somador_2_1_cout));
endmodule

module somador_8 (
  input  [7:0] A,
  input  [7:0] b,
  output S0,
  output S1,
  output S2,
  output S3,
  output S4,
  output S5,
  output S6,
  output S7,
  output Cout
);

  wire somador_4_1_cout;

  somador_4 somador_4_1 (
    .A0(A[0]), .A1(A[1]), .A2(A[2]), .A3(A[3]), .B0(b[0]), .B1(b[1]), .B2(b[2]), .B3(b[3]), .Cin(1'b0),
    .S0(S0), .S1(S1), .S2(S2), .S3(S3), .Cout(somador_4_1_cout));
  somador_4 somador_4_2 (
    .A0(A[4]), .A1(A[5]), .A2(A[6]), .A3(A[7]), .B0(b[4]), .B1(b[5]), .B2(b[6]), .B3(b[7]),
    .Cin(somador_4_1_cout), .S0(S4), .S1(S5), .S2(S6), .S3(S7), .Cout(Cout));
endmodule
